// Logisim project lab04.circ as structural Verilog: 13 circuits, main circuit main
module main (
  input  [3:0] OP,
  input  Cin,
  input  [7:0] A,
  input  [7:0] B,
  output OF,
  output Cout,
  output [7:0] F,
  output SF,
  output ZF
);

  ALU alu_1 (.OP(OP), .Cin(Cin), .A(A), .B(B), .OF(OF), .Cout(Cout), .F(F), .ZF(ZF), .SF(SF));
endmodule

module _1_bit_add (
  input  A,
  input  B,
  input  C,
  output F,
  output Cout
);

  wire and_1_out, and_2_out, xor_1_out;

  xor xor_1 (xor_1_out, A, B);
  and and_1 (and_1_out, A, B);
  and and_2 (and_2_out, xor_1_out, C);
  xor xor_2 (F, xor_1_out, C);
  or or_1 (Cout, and_2_out, and_1_out);
endmodule

module _4_bit_add (
  input  [3:0] in_1,
  input  [3:0] in_2,
  input  cin,
  output [3:0] F,
  output out_5
);

  wire n1_bit_add_1_cout, n1_bit_add_2_cout, n1_bit_add_3_cout;

  _1_bit_add u_1_bit_add_1 (.A(in_1[0]), .B(in_2[0]), .C(cin), .F(F[0]), .Cout(n1_bit_add_1_cout));
  _1_bit_add u_1_bit_add_2 (.A(in_1[1]), .B(in_2[1]), .C(n1_bit_add_1_cout), .F(F[1]), .Cout(n1_bit_add_2_cout));
  _1_bit_add u_1_bit_add_3 (.A(in_1[2]), .B(in_2[2]), .C(n1_bit_add_2_cout), .F(F[2]), .Cout(n1_bit_add_3_cout));
  _1_bit_add u_1_bit_add_4 (.A(in_1[3]), .B(in_2[3]), .C(n1_bit_add_3_cout), .F(F[3]), .Cout(out_5));
endmodule

// ADD
module _8_bit_add (
  input  [7:0] A,
  input  [7:0] B,
  input  Cin,
  output OF,
  output [7:0] F,
  output Cout
);

  wire n4_bit_add_1_out_5;

  overflow overflow_1 (.A7(A[7]), .B7(B[7]), .F7(F[7]), .OF(OF));
  _4_bit_add u_4_bit_add_1 (.in_1(A[3:0]), .in_2(B[3:0]), .cin(Cin), .F(F[3:0]), .out_5(n4_bit_add_1_out_5));
  _4_bit_add u_4_bit_add_2 (.in_1(A[7:4]), .in_2(B[7:4]), .cin(n4_bit_add_1_out_5), .F(F[7:4]), .out_5(Cout));
endmodule

// SUB
module sub (
  input  cin,
  input  [7:0] A,
  input  [7:0] B,
  output OF,
  output cout,
  output [7:0] out_6
);

  wire [7:0] n8_bit_add_1_f, not_1_out;

  assign not_1_out = ~B;  // NOT_Gate not_1, 8 bits wide
  overflow overflow_1 (.A7(not_1_out[7]), .B7(A[7]), .F7(out_6[7]), .OF(OF));
  _8_bit_add u_8_bit_add_1 (.A({8{1'b0}}), .B(not_1_out), .Cin(1'b0), .F(n8_bit_add_1_f));  // open: OF, Cout
  _8_bit_add u_8_bit_add_2 (.A(A), .B(n8_bit_add_1_f), .Cin(cin), .F(out_6), .Cout(cout));  // open: OF
endmodule

// AND
module bitand (
  input  [7:0] A,
  input  [7:0] B,
  output [7:0] F
);

  assign F = A & B;  // AND_Gate and_1, 8 bits wide
endmodule

// XOR
module bitwise_XOR (
  input  [7:0] in_1,
  input  [7:0] in_2,
  output [7:0] F
);

  assign F = in_1 ^ in_2;  // XOR_Gate xor_1, 8 bits wide
endmodule

// RST
module rShift (
  input  [7:0] A,
  output Cout,
  output [7:0] F
);


  assign Cout = A[0];
  assign F = {1'b0, A[7:1]};
endmodule

// LST
module lShift (
  input  [7:0] A,
  output [7:0] F,
  output Cout
);


  assign Cout = A[7];
  assign F = {A[6:0], 1'b0};
endmodule

// ALU8
module ALU (
  input  [3:0] OP,
  input  Cin,
  input  [7:0] A,
  input  [7:0] B,
  output OF,
  output Cout,
  output [7:0] F,
  output ZF,
  output SF
);

  wire lshift_1_cout, n8_bit_add_1_cout, n8_bit_add_1_of, rshift_1_cout, sub_1_cout, sub_1_of;
  wire [7:0] bitand_1_f, bitwise_xor_1_f, lshift_1_f, n8_bit_add_1_f, rshift_1_f, sub_1_out_6;

  Multiplexer #(.select(4), .enable("false")) multiplexer_1 (
    .in0(n8_bit_add_1_of), .in1(sub_1_of), .in2(1'b0), .in3(1'b0), .in4(1'b0), .out(OF), .sel(OP));  // open: in5, in6, in7, in8, in9, in10, in11, in12, in13, in14, in15
  _8_bit_add u_8_bit_add_1 (
    .A(A), .B(B), .Cin(Cin), .OF(n8_bit_add_1_of), .F(n8_bit_add_1_f), .Cout(n8_bit_add_1_cout));
  sub sub_1 (.cin(Cin), .A(A), .B(B), .OF(sub_1_of), .cout(sub_1_cout), .out_6(sub_1_out_6));
  Multiplexer #(.select(4), .width(8), .enable("false")) multiplexer_2 (
    .in0(n8_bit_add_1_f), .in1(sub_1_out_6), .in2(bitand_1_f), .in3(bitwise_xor_1_f), .in4(rshift_1_f),
    .in5(lshift_1_f), .out(F), .sel(OP));  // open: in6, in7, in8, in9, in10, in11, in12, in13, in14, in15
  bitand bitand_1 (.A(A), .B(B), .F(bitand_1_f));
  Multiplexer #(.select(4), .enable("false")) multiplexer_3 (
    .in0(n8_bit_add_1_cout), .in1(sub_1_cout), .in2(1'b0), .in3(1'b0), .in4(rshift_1_cout),
    .in5(lshift_1_cout), .out(Cout), .sel(OP));  // open: in6, in7, in8, in9, in10, in11, in12, in13, in14, in15
  bitwise_XOR bitwise_xor_1 (.in_1(A), .in_2(B), .F(bitwise_xor_1_f));
  rShift rshift_1 (.A(A), .Cout(rshift_1_cout), .F(rshift_1_f));
  lShift lshift_1 (.A(A), .Cout(lshift_1_cout), .F(lshift_1_f));
  flagers flagers_1 (.F(F), .ZF(ZF), .SF(SF));
endmodule

// OF
module overflow (
  input  A7,
  input  B7,
  input  F7,
  output OF
);

  wire not_1_out, xor_1_out, xor_2_out;

  xor xor_1 (xor_1_out, A7, B7);
  xor xor_2 (xor_2_out, B7, F7);
  not not_1 (not_1_out, xor_1_out);
  and and_1 (OF, not_1_out, xor_2_out);
endmodule

// FLG
module flagers (
  input  [7:0] F,
  output ZF,
  output SF
);

  wire or_1_out;

  or or_1 (or_1_out, F[0], F[1], F[2], F[3], F[4], F[5], F[6], F[7]);
  not not_1 (ZF, or_1_out);

  assign SF = F[7];
endmodule

module _32_bit_ALU (
  input  in_1,
  input  [3:0] OP,
  input  [31:0] B,
  input  [31:0] A,
  output [31:0] F,
  output ZF,
  output OF,
  output Cout,
  output SF
);

  wire alu_1_cout, alu_1_zf, alu_2_cout, alu_2_zf, alu_3_cout, alu_3_zf, alu_4_zf;

  ALU alu_1 (
    .OP(OP), .Cin(in_1), .A(B[7:0]), .B(A[7:0]), .Cout(alu_1_cout), .F(F[7:0]), .ZF(alu_1_zf));  // open: OF, SF
  ALU alu_2 (
    .OP(OP), .Cin(alu_1_cout), .A(B[15:8]), .B(A[15:8]), .Cout(alu_2_cout), .F(F[15:8]), .ZF(alu_2_zf));  // open: OF, SF
  ALU alu_3 (
    .OP(OP), .Cin(alu_2_cout), .A(B[23:16]), .B(A[23:16]), .Cout(alu_3_cout), .F(F[23:16]), .ZF(alu_3_zf));  // open: OF, SF
  ALU alu_4 (
    .OP(OP), .Cin(alu_3_cout), .A(B[31:24]), .B(A[31:24]), .OF(OF), .Cout(Cout), .F(F[31:24]), .ZF(alu_4_zf),
    .SF(SF));
  and and_1 (ZF, alu_1_zf, alu_2_zf, alu_3_zf, alu_4_zf);
endmodule
