// Logisim project regs.circ as structural Verilog: 5 circuits, main circuit regfile
module regfile (
  input  [3:0] srcA,
  input  [3:0] srcB,
  input  [3:0] dstE,
  input  [31:0] valE_1,
  input  [31:0] valE_0,
  input  [3:0] dstM,
  input  [31:0] valM_1,
  input  [31:0] valM_0,
  input  in_9,
  input  in_10,
  output [31:0] valA_1,
  output [31:0] valA_0,
  output [31:0] valB_1,
  output [31:0] valB_0
);

  wire and_1_out, and_2_out, and_3_out, and_4_out, msb4_1_msb, msb4_2_msb, msb4_3_msb, msb4_4_msb,
       regwriteenable_1_enable, regwriteenable_2_enable;
  wire [2:0] msb4_1_lower3, msb4_2_lower3, msb4_3_lower3, msb4_4_lower3;
  wire [31:0] regs8x32_1_vala, regs8x32_1_valb, regs8x32_2_vala, regs8x32_2_valb, regs8x32_3_vala,
       regs8x32_3_valb, regs8x32_4_vala, regs8x32_4_valb;

  msb4 msb4_1 (.in_1(srcA), .msb(msb4_1_msb), .lower3(msb4_1_lower3));
  msb4 msb4_2 (.in_1(srcB), .msb(msb4_2_msb), .lower3(msb4_2_lower3));
  regwriteenable regwriteenable_1 (.\reg (dstE), .enable(regwriteenable_1_enable));
  msb4 msb4_3 (.in_1(dstE), .msb(msb4_3_msb), .lower3(msb4_3_lower3));
  regwriteenable regwriteenable_2 (.\reg (dstM), .enable(regwriteenable_2_enable));
  msb4 msb4_4 (.in_1(dstM), .msb(msb4_4_msb), .lower3(msb4_4_lower3));
  and and_1 (and_1_out, regwriteenable_1_enable, ~msb4_3_msb);  // AND_Gate
  and and_2 (and_2_out, regwriteenable_1_enable, msb4_3_msb);
  and and_3 (and_3_out, regwriteenable_2_enable, ~msb4_4_msb);  // AND_Gate
  and and_4 (and_4_out, regwriteenable_2_enable, msb4_4_msb);
  Regs8x32 regs8x32_1 (
    .srcA(msb4_1_lower3), .srcB(msb4_2_lower3), .dstEenable(and_1_out), .dstE(msb4_3_lower3), .valE(valE_1),
    .dstMenable(and_3_out), .dstM(msb4_4_lower3), .valM(valM_1), .Clock(in_9), .Clear(in_10),
    .valA(regs8x32_1_vala), .valB(regs8x32_1_valb));
  Regs8x32 regs8x32_2 (
    .srcA(msb4_1_lower3), .srcB(msb4_2_lower3), .dstEenable(and_1_out), .dstE(msb4_3_lower3), .valE(valE_0),
    .dstMenable(and_3_out), .dstM(msb4_4_lower3), .valM(valM_0), .Clock(in_9), .Clear(in_10),
    .valA(regs8x32_2_vala), .valB(regs8x32_2_valb));
  Regs8x32 regs8x32_3 (
    .srcA(msb4_1_lower3), .srcB(msb4_2_lower3), .dstEenable(and_2_out), .dstE(msb4_3_lower3), .valE(valE_1),
    .dstMenable(and_4_out), .dstM(msb4_4_lower3), .valM(valM_1), .Clock(in_9), .Clear(in_10),
    .valA(regs8x32_3_vala), .valB(regs8x32_3_valb));
  Regs8x32 regs8x32_4 (
    .srcA(msb4_1_lower3), .srcB(msb4_2_lower3), .dstEenable(and_2_out), .dstE(msb4_3_lower3), .valE(valE_0),
    .dstMenable(and_4_out), .dstM(msb4_4_lower3), .valM(valM_0), .Clock(in_9), .Clear(in_10),
    .valA(regs8x32_4_vala), .valB(regs8x32_4_valb));
  Multiplexer #(.width(32), .enable("false")) multiplexer_1 (
    .in0(regs8x32_1_vala), .in1(regs8x32_3_vala), .out(valA_1), .sel(msb4_1_msb));
  Multiplexer #(.width(32), .enable("false")) multiplexer_2 (
    .in0(regs8x32_2_vala), .in1(regs8x32_4_vala), .out(valA_0), .sel(msb4_1_msb));
  Multiplexer #(.width(32), .enable("false")) multiplexer_3 (
    .in0(regs8x32_1_valb), .in1(regs8x32_3_valb), .out(valB_1), .sel(msb4_2_msb));
  Multiplexer #(.width(32), .enable("false")) multiplexer_4 (
    .in0(regs8x32_2_valb), .in1(regs8x32_4_valb), .out(valB_0), .sel(msb4_2_msb));

  // Notes on the sheet:
  //   Regs0-7MS
  //   Regs0-7LS
  //   Regs8-15MS
  //   Regs8-15LS
endmodule

module Regs8x32 (
  input  [2:0] srcA,
  input  [2:0] srcB,
  input  dstEenable,
  input  [2:0] dstE,
  input  [31:0] valE,
  input  dstMenable,
  input  [2:0] dstM,
  input  [31:0] valM,
  input  Clock,
  input  Clear,
  output [31:0] valA,
  output [31:0] valB
);

  wire demultiplexer_1_out0, demultiplexer_1_out1, demultiplexer_1_out2, demultiplexer_1_out3,
       demultiplexer_1_out4, demultiplexer_1_out5, demultiplexer_1_out6, demultiplexer_1_out7,
       demultiplexer_2_out0, demultiplexer_2_out1, demultiplexer_2_out2, demultiplexer_2_out3,
       demultiplexer_2_out4, demultiplexer_2_out5, demultiplexer_2_out6, demultiplexer_2_out7,
       regwrite_1_enable, regwrite_2_enable, regwrite_3_enable, regwrite_4_enable, regwrite_5_enable,
       regwrite_6_enable, regwrite_7_enable, regwrite_8_enable;
  wire [31:0] register_1_q, register_2_q, register_3_q, register_4_q, register_5_q, register_6_q,
       register_7_q, register_8_q, regwrite_1_data, regwrite_2_data, regwrite_3_data, regwrite_4_data,
       regwrite_5_data, regwrite_6_data, regwrite_7_data, regwrite_8_data;

  Demultiplexer #(.select(3), .enable("false")) demultiplexer_1 (
    .out0(demultiplexer_1_out0), .out1(demultiplexer_1_out1), .out2(demultiplexer_1_out2),
    .out3(demultiplexer_1_out3), .out4(demultiplexer_1_out4), .out5(demultiplexer_1_out5),
    .out6(demultiplexer_1_out6), .out7(demultiplexer_1_out7), .in(dstEenable), .sel(dstE));
  Demultiplexer #(.select(3), .enable("false")) demultiplexer_2 (
    .out0(demultiplexer_2_out0), .out1(demultiplexer_2_out1), .out2(demultiplexer_2_out2),
    .out3(demultiplexer_2_out3), .out4(demultiplexer_2_out4), .out5(demultiplexer_2_out5),
    .out6(demultiplexer_2_out6), .out7(demultiplexer_2_out7), .in(dstMenable), .sel(dstM));
  RegWrite regwrite_1 (
    .dstE(demultiplexer_1_out0), .dstM(demultiplexer_2_out0), .valE(valE), .valM(valM),
    .Data(regwrite_1_data), .Enable(regwrite_1_enable));
  RegWrite regwrite_2 (
    .dstE(demultiplexer_1_out1), .dstM(demultiplexer_2_out1), .valE(valE), .valM(valM),
    .Data(regwrite_2_data), .Enable(regwrite_2_enable));
  RegWrite regwrite_3 (
    .dstE(demultiplexer_1_out2), .dstM(demultiplexer_2_out2), .valE(valE), .valM(valM),
    .Data(regwrite_3_data), .Enable(regwrite_3_enable));
  RegWrite regwrite_4 (
    .dstE(demultiplexer_1_out3), .dstM(demultiplexer_2_out3), .valE(valE), .valM(valM),
    .Data(regwrite_4_data), .Enable(regwrite_4_enable));
  RegWrite regwrite_5 (
    .dstE(demultiplexer_1_out4), .dstM(demultiplexer_2_out4), .valE(valE), .valM(valM),
    .Data(regwrite_5_data), .Enable(regwrite_5_enable));
  RegWrite regwrite_6 (
    .dstE(demultiplexer_1_out5), .dstM(demultiplexer_2_out5), .valE(valE), .valM(valM),
    .Data(regwrite_6_data), .Enable(regwrite_6_enable));
  RegWrite regwrite_7 (
    .dstE(demultiplexer_1_out6), .dstM(demultiplexer_2_out6), .valE(valE), .valM(valM),
    .Data(regwrite_7_data), .Enable(regwrite_7_enable));
  RegWrite regwrite_8 (
    .dstE(demultiplexer_1_out7), .dstM(demultiplexer_2_out7), .valE(valE), .valM(valM),
    .Data(regwrite_8_data), .Enable(regwrite_8_enable));
  Register #(.width(32)) register_1 (
    .D(regwrite_1_data), .en(regwrite_1_enable), .Q(register_1_q), .clk(Clock), .clr(Clear));
  Register #(.width(32)) register_2 (
    .D(regwrite_2_data), .en(regwrite_2_enable), .Q(register_2_q), .clk(Clock), .clr(Clear));
  Register #(.width(32)) register_3 (
    .D(regwrite_3_data), .en(regwrite_3_enable), .Q(register_3_q), .clk(Clock), .clr(Clear));
  Register #(.width(32)) register_4 (
    .D(regwrite_4_data), .en(regwrite_4_enable), .Q(register_4_q), .clk(Clock), .clr(Clear));
  Register #(.width(32)) register_5 (
    .D(regwrite_5_data), .en(regwrite_5_enable), .Q(register_5_q), .clk(Clock), .clr(Clear));
  Register #(.width(32)) register_6 (
    .D(regwrite_6_data), .en(regwrite_6_enable), .Q(register_6_q), .clk(Clock), .clr(Clear));
  Register #(.width(32)) register_7 (
    .D(regwrite_7_data), .en(regwrite_7_enable), .Q(register_7_q), .clk(Clock), .clr(Clear));
  Register #(.width(32)) register_8 (
    .D(regwrite_8_data), .en(regwrite_8_enable), .Q(register_8_q), .clk(Clock), .clr(Clear));
  Multiplexer #(.select(3), .width(32), .enable("false")) multiplexer_1 (
    .in0(register_1_q), .in1(register_2_q), .in2(register_3_q), .in3(register_4_q), .in4(register_5_q),
    .in5(register_6_q), .in6(register_7_q), .in7(register_8_q), .out(valA), .sel(srcA));
  Multiplexer #(.select(3), .width(32), .enable("false")) multiplexer_2 (
    .in0(register_1_q), .in1(register_2_q), .in2(register_3_q), .in3(register_4_q), .in4(register_5_q),
    .in5(register_6_q), .in6(register_7_q), .in7(register_8_q), .out(valB), .sel(srcB));
endmodule

module RegWrite (
  input  dstE,
  input  dstM,
  input  [31:0] valE,
  input  [31:0] valM,
  output [31:0] Data,
  output Enable
);

  or or_1 (Enable, dstE, dstM);
  Multiplexer #(.width(32), .enable("false")) multiplexer_1 (.in0(valE), .in1(valM), .out(Data), .sel(dstM));
endmodule

module msb4 (
  input  [3:0] in_1,
  output msb,
  output [2:0] lower3
);


  assign lower3 = in_1[2:0];
  assign msb = in_1[3];
endmodule

module regwriteenable (
  input  [3:0] \reg ,
  output enable
);

  wire and_1_out;

  not not_1 (enable, and_1_out);
  and and_1 (and_1_out, \reg [3], \reg [2], \reg [1], \reg [0]);
endmodule
