// Logisim project y86.circ as structural Verilog: 15 circuits, main circuit main
module main (
  input  in_1,
  input  Reset,
  output [3:0] out_3,
  output [31:0] out_4,
  output [3:0] out_5,
  output [31:0] out_6,
  output [31:0] out_7
);

  wire and_1_out, CC, Clock_out, dememrr, imemrr, ins_inv, memory_1_read, memory_1_write, nor_1_out,
       not_1_out;
  wire [1:0] stat_helper_statuscode, Stat_q;
  wire [3:0] decode_1_deste, decode_1_destm, decode_1_srca, decode_1_srcb, fetch_1_ra, fetch_1_rb;
  wire [31:0] fetch_1_val_c1, memory_1_addr_0, memory_1_addr_1, memory_1_data_0, memory_1_data_1, PC_q,
       PChold_q, regfile_1_vala_1, regfile_1_valb_0, regfile_1_valb_1, ValE_0, ValE_1, ValM_0, ValM_1;

  and and_1 (and_1_out, Clock_out, nor_1_out);
  Clock Clock (.out(Clock_out));
  Register #(.width(32)) PC (.D(PChold_q), .Q(PC_q), .clk(and_1_out), .clr(Reset));  // open: en
  nor nor_1 (nor_1_out, Stat_q[1], Stat_q[0]);
  Fetch fetch_1 (
    .PC(PC_q), .invalid_ins(ins_inv), .iFun(out_5), .iCode(out_3), .rA(fetch_1_ra), .rB(fetch_1_rb),
    .imemerror(imemrr), .Val_P(out_6), .Val_C0(out_7), .Val_C1(fetch_1_val_c1));
  not not_1 (not_1_out, and_1_out);
  Register #(.width(2)) Stat (.D(stat_helper_statuscode), .Q(Stat_q), .clk(not_1_out));  // open: en, clr
  Decode decode_1 (
    .rA(fetch_1_ra), .iCode(out_3), .rB(fetch_1_rb), .srcB(decode_1_srcb), .destM(decode_1_destm),
    .srcA(decode_1_srca), .destE(decode_1_deste));
  stat_helper stat_helper (
    .ins_inv(ins_inv), .imemrr(imemrr), .dmemrr(dememrr), .icode(out_3), .statuscode(stat_helper_statuscode));
  Execute execute_1 (
    .ValA_0(regfile_1_vala_1), .ValB_0(regfile_1_valb_0), .ValC_0(out_7), .ValA_1(regfile_1_vala_1),
    .ValB_1(regfile_1_valb_1), .ValC_1(fetch_1_val_c1), .iFun(out_5), .iCode(out_3), .in_2(in_1),
    .ValE_0(ValE_0), .ValE_1(ValE_1), .CC(CC));
  regfile regfile_1 (
    .srcA(decode_1_srca), .srcB(decode_1_srcb), .dstE(decode_1_deste), .valE_1(ValE_1), .valE_0(ValE_0),
    .dstM(decode_1_destm), .valM_1(ValM_1), .valM_0(ValM_0), .valA_1(regfile_1_vala_1),
    .valA_0(regfile_1_vala_1), .valB_1(regfile_1_valb_1), .valB_0(regfile_1_valb_0), .in_9(not_1_out),
    .in_10(Reset));
  Memory memory_1 (
    .ValE_0(ValE_0), .ValE_1(ValE_1), .ValA_0(regfile_1_vala_1), .ValA_1(regfile_1_vala_1), .ValP(out_6),
    .iCode(out_3), .Read(memory_1_read), .Write(memory_1_write), .Addr_0(memory_1_addr_0),
    .Data_0(memory_1_data_0), .Addr_1(memory_1_addr_1), .Data_1(memory_1_data_1));
  dmem dmem_1 (
    .Addr_1(memory_1_addr_1), .Addr_0(memory_1_addr_0), .Data_1(memory_1_data_1), .Data_0(memory_1_data_0),
    .read(memory_1_read), .write(memory_1_write), .valM_1(ValM_1), .valM_0(ValM_0), .dmemerr(dememrr),
    .clock(not_1_out), .dataclear(Reset));
  PC pc_2 (.ValP(out_6), .ValC_0(out_7), .ValM_0(ValM_0), .CC(CC), .iCode(out_3), .NextPC_0(out_4));
  Register #(.width(32)) PChold (.D(out_4), .en(1'b1), .Q(PChold_q), .clk(not_1_out), .clr(Reset));

  // Other names for the same wires on the sheet: iCode[3:0] = out_3; iFun[3:0] = out_5; NextPC_0[31:0] = out_4;
  //   ValC_0[31:0] = out_7; ValP[31:0] = out_6
endmodule

module Align (
  input  [7:0] B1,
  input  [7:0] B2,
  input  [7:0] B3,
  input  [7:0] B4,
  input  [7:0] B5,
  input  [7:0] B6,
  input  [7:0] B7,
  input  [7:0] B8,
  input  [7:0] B9,
  input  NeedRegs,
  input  NeedValc,
  output [3:0] rA,
  output [3:0] rB,
  output [31:0] valC_1,
  output [31:0] valC_0
);

  wire [31:0] multiplexer_1_out, multiplexer_3_out;

  Multiplexer #(.width(32)) multiplexer_1 (
    .in0({B8, B7, B6, B5}), .in1({B9, B8, B7, B6}), .out(multiplexer_1_out), .sel(NeedRegs));  // open: en
  Multiplexer #(.width(4)) multiplexer_2 (.in0(4'b1111), .in1(B1[3:0]), .out(rB), .sel(NeedRegs));  // open: en
  Multiplexer #(.width(32)) multiplexer_3 (
    .in0({B4, B3, B2, B1}), .in1({B5, B4, B3, B2}), .out(multiplexer_3_out), .sel(NeedRegs));  // open: en
  Multiplexer #(.width(4)) multiplexer_4 (.in0(4'b1111), .in1(B1[7:4]), .out(rA), .sel(NeedRegs));  // open: en
  Multiplexer #(.width(32)) multiplexer_5 (
    .in0({32{1'b0}}), .in1(multiplexer_3_out), .out(valC_0), .sel(NeedValc));  // open: en
  Multiplexer #(.width(32)) multiplexer_6 (
    .in0({32{1'b0}}), .in1(multiplexer_1_out), .out(valC_1), .sel(NeedValc));  // open: en
endmodule

module Fetch (
  input  [31:0] PC,
  output invalid_ins,
  output [3:0] iFun,
  output [3:0] iCode,
  output [3:0] rA,
  output [3:0] rB,
  output [31:0] Val_P,
  output [31:0] Val_C0,
  output [31:0] Val_C1,
  output imemerror
);

  wire split_1_needs_reg, split_1_needs_valc;
  wire [7:0] imem_1_out_2, imem_1_out_3, imem_1_out_4, imem_1_out_5, imem_1_out_6, imem_1_out_7,
       imem_1_out_8, imem_1_out_9, imem_1_out_10, imem_1_out_12;
  wire [31:0] multiplexer_1_out;

  imem imem_1 (
    .in_1(PC), .imemerr(imemerror), .out_2(imem_1_out_2), .out_3(imem_1_out_3), .out_4(imem_1_out_4),
    .out_5(imem_1_out_5), .out_6(imem_1_out_6), .out_7(imem_1_out_7), .out_8(imem_1_out_8),
    .out_9(imem_1_out_9), .out_10(imem_1_out_10), .out_12(imem_1_out_12));
  split split_1 (
    .in_1(imem_1_out_2), .ifun(iFun), .icode(iCode), .Invalid_inst(invalid_ins),
    .Needs_reg(split_1_needs_reg), .needs_valc(split_1_needs_valc));
  Align Align (
    .B1(imem_1_out_3), .B2(imem_1_out_4), .B3(imem_1_out_5), .B4(imem_1_out_6), .B5(imem_1_out_7),
    .B6(imem_1_out_8), .B7(imem_1_out_9), .B8(imem_1_out_10), .B9(imem_1_out_12),
    .NeedRegs(split_1_needs_reg), .NeedValc(split_1_needs_valc), .rA(rA), .rB(rB), .valC_1(Val_C1),
    .valC_0(Val_C0));
  Multiplexer #(.width(32)) multiplexer_1 (
    .in0(32'h1), .in1(32'h9), .out(multiplexer_1_out), .sel(split_1_needs_valc));  // open: en
  _32_bit_ALU u_32_bit_alu_1 (
    .in_1(split_1_needs_reg), .OP(4'b0000), .B(multiplexer_1_out), .A(PC), .F(Val_P));  // open: OF, Cout, SF, ZF
endmodule

module split (
  input  [7:0] in_1,
  output [3:0] ifun,
  output [3:0] icode,
  output Invalid_inst,
  output Needs_reg,
  output needs_valc
);

  wire and_1_out, and_2_out, and_3_out, and_4_out, and_5_out, not_1_out, not_2_out, not_3_out, not_4_out,
       xor_1_out;

  not not_1 (not_1_out, in_1[4]);
  not not_2 (not_2_out, in_1[5]);
  not not_3 (not_3_out, in_1[4]);
  not not_4 (not_4_out, in_1[7]);
  and and_1 (and_1_out, not_1_out, in_1[5]);
  and and_2 (and_2_out, not_2_out, in_1[6]);
  and and_3 (and_3_out, in_1[5], in_1[4], not_4_out);
  xor xor_1 (xor_1_out, in_1[5], in_1[6]);
  and and_4 (and_4_out, in_1[7], not_2_out, not_3_out);
  and and_5 (and_5_out, in_1[4], in_1[6]);
  and and_6 (Invalid_inst, in_1[6], in_1[7]);
  or or_1 (Needs_reg, and_1_out, xor_1_out);
  or or_2 (needs_valc, and_2_out, and_5_out, and_4_out, and_3_out);

  assign icode = in_1[7:4];
  assign ifun = in_1[3:0];
endmodule

module Decode (
  input  [3:0] rA,
  input  [3:0] iCode,
  input  [3:0] rB,
  output [3:0] srcA,
  output [3:0] destE,
  output [3:0] srcB,
  output [3:0] destM
);

  Multiplexer #(.select(4), .width(4)) multiplexer_1 (
    .in0(4'b1111), .in1(4'b1111), .in2(rB), .in3(4'b1111), .in4(rB), .in5(rB), .in6(rB), .in7(rB),
    .in8(4'b0100), .in9(4'b0100), .in10(4'b0100), .in11(4'b0100), .in12(4'b1111), .in13(4'b1111),
    .in14(4'b1111), .in15(4'b1111), .out(srcB), .sel(iCode));  // open: en
  Multiplexer #(.select(4), .width(4)) multiplexer_2 (
    .in0(rA), .in1(rA), .in2(rA), .in3(rA), .in4(rA), .in5(4'b1111), .in6(rA), .in7(rA), .in8(rA),
    .in9(4'b0100), .in10(rA), .in11(4'b0100), .in12(4'b1111), .in13(4'b1111), .in14(4'b1111), .in15(4'b1111),
    .out(srcA), .sel(iCode));  // open: en
  Multiplexer #(.select(4), .width(4)) multiplexer_3 (
    .in0(4'b1111), .in1(4'b1111), .in2(rB), .in3(rB), .in4(4'b1111), .in5(4'b1111), .in6(rB), .in7(4'b1111),
    .in8(4'b0100), .in9(4'b0100), .in10(4'b0100), .in11(4'b0100), .in12(4'b1111), .in13(4'b1111),
    .in14(4'b1111), .in15(4'b1111), .out(destE), .sel(iCode));  // open: en
  Multiplexer #(.select(4), .width(4)) multiplexer_4 (
    .in0(4'b1111), .in1(4'b1111), .in2(4'b1111), .in3(4'b1111), .in4(4'b1111), .in5(rA), .in6(4'b1111),
    .in7(4'b1111), .in8(4'b1111), .in9(4'b1111), .in10(4'b1111), .in11(rA), .in12(4'b1111), .in13(4'b1111),
    .in14(4'b1111), .in15(4'b1111), .out(destM), .sel(iCode));  // open: en
endmodule

// ALU
module _64_bit (
  input  [3:0] OP,
  input  Cin,
  input  [31:0] A,
  input  [31:0] B,
  input  [31:0] A_2,
  input  [31:0] B_2,
  output [31:0] F,
  output ZF,
  output [31:0] F_2,
  output OF,
  output SF,
  output Cout
);

  wire and_2_out, multiplexer_1_out, n32_bit_alu_1_cout, n32_bit_alu_1_zf, n32_bit_alu_2_zf, not_1_out,
       not_2_out, not_3_out;

  _32_bit_ALU u_32_bit_alu_1 (
    .in_1(multiplexer_1_out), .OP(OP), .B(B), .A(A), .Cout(n32_bit_alu_1_cout), .F(F), .ZF(n32_bit_alu_1_zf));  // open: OF, SF
  _32_bit_ALU u_32_bit_alu_2 (
    .in_1(n32_bit_alu_1_cout), .OP(OP), .B(B_2), .A(A_2), .OF(OF), .Cout(Cout), .SF(SF), .F(F_2),
    .ZF(n32_bit_alu_2_zf));
  Multiplexer multiplexer_1 (.in0(Cin), .in1(1'b1), .out(multiplexer_1_out), .sel(and_2_out));  // open: en
  not not_1 (not_1_out, OP[1]);
  not not_2 (not_2_out, OP[2]);
  not not_3 (not_3_out, OP[3]);
  and and_1 (ZF, n32_bit_alu_1_zf, n32_bit_alu_2_zf);
  and and_2 (and_2_out, OP[0], not_1_out, not_2_out, not_3_out);
endmodule

module Execute (
  input  [31:0] ValA_0,
  input  in_2,
  input  [31:0] ValB_0,
  input  [31:0] ValC_0,
  input  [31:0] ValA_1,
  input  [31:0] ValB_1,
  input  [31:0] ValC_1,
  input  [3:0] iFun,
  input  [3:0] iCode,
  output [31:0] ValE_0,
  output [31:0] ValE_1,
  output CC
);

  wire and_1_out, clock_1_out, n64_bit_1_of, n64_bit_1_sf, n64_bit_1_zf, not_1_out, not_2_out,
       subcircuit_1_q, subcircuit_2_q, subcircuit_3_q;
  wire [3:0] multiplexer_1_out;
  wire [31:0] helper_execute_1_a, helper_execute_1_b, helper_execute_2_a, helper_execute_2_b;

  helper_execute helper_execute_1 (
    .ValA(ValA_1), .ValB(ValB_1), .ValC(ValC_1), .icode(iCode), .A(helper_execute_1_a), .B(helper_execute_1_b));
  helper_execute helper_execute_2 (
    .ValA(ValA_0), .ValB(ValB_0), .ValC(ValC_0), .icode(iCode), .A(helper_execute_2_a), .B(helper_execute_2_b));
  Multiplexer #(.select(4), .width(4)) multiplexer_1 (
    .in0(4'b0000), .in1(4'b0000), .in2(4'b0000), .in3(4'b0000), .in4(4'b0000), .in5(4'b0000), .in6(iFun),
    .in7(4'b0000), .in8(4'b0000), .in9(4'b0000), .in10(4'b0000), .in11(4'b0000), .in12(4'b0000),
    .in13(4'b0000), .in14(4'b0000), .in15(4'b0000), .out(multiplexer_1_out), .sel(iCode));  // open: en
  _64_bit u_64_bit_1 (
    .A(helper_execute_2_a), .B(helper_execute_2_b), .A_2(helper_execute_1_a), .B_2(helper_execute_1_b),
    .OP(multiplexer_1_out), .Cin(in_2), .OF(n64_bit_1_of), .F(ValE_0), .ZF(n64_bit_1_zf), .F_2(ValE_1),
    .SF(n64_bit_1_sf));  // open: Cout
  subcircuit subcircuit_1 (.A(and_1_out), .B(n64_bit_1_zf), .CLK(clock_1_out), .Q(subcircuit_1_q));
  subcircuit subcircuit_2 (.A(and_1_out), .B(n64_bit_1_sf), .CLK(clock_1_out), .Q(subcircuit_2_q));
  subcircuit subcircuit_3 (.A(and_1_out), .B(n64_bit_1_of), .CLK(clock_1_out), .Q(subcircuit_3_q));
  not not_1 (not_1_out, iCode[0]);
  not not_2 (not_2_out, iCode[3]);
  Clock clock_1 (.out(clock_1_out));
  and and_1 (and_1_out, not_1_out, iCode[1], iCode[2], not_2_out);
  CC cc_1 (.ZF(subcircuit_1_q), .OF(subcircuit_3_q), .SF(subcircuit_2_q), .ifun(iFun), .CC(CC));
endmodule

module helper_execute (
  input  [31:0] ValA,
  input  [31:0] ValB,
  input  [31:0] ValC,
  input  [3:0] icode,
  output [31:0] A,
  output [31:0] B
);

  Multiplexer #(.select(4), .width(32)) multiplexer_1 (
    .in0({32{1'b0}}), .in1({32{1'b0}}), .in2(ValA), .in3(ValC), .in4(ValC), .in5(ValC), .in6(ValA),
    .in7(ValC), .in8(32'hfffffff8), .in9(32'h8), .in10(32'hfffffff8), .in11(32'h8), .in12({32{1'b0}}),
    .in13({32{1'b0}}), .in14({32{1'b0}}), .in15({32{1'b0}}), .out(A), .sel(icode));  // open: en
  Multiplexer #(.select(4), .width(32)) multiplexer_2 (
    .in0({32{1'b0}}), .in1({32{1'b0}}), .in2({32{1'b0}}), .in3({32{1'b0}}), .in4(ValB), .in5(ValB),
    .in6(ValB), .in7({32{1'b0}}), .in8(ValB), .in9(ValB), .in10(ValB), .in11(ValB), .in12({32{1'b0}}),
    .in13({32{1'b0}}), .in14({32{1'b0}}), .in15({32{1'b0}}), .out(B), .sel(icode));  // open: en
endmodule

module CC (
  input  ZF,
  input  OF,
  input  SF,
  input  [3:0] ifun,
  output CC
);

  wire and_1_out, not_1_out, not_2_out, not_3_out, or_1_out, xor_1_out;

  or or_1 (or_1_out, ZF, xor_1_out);
  xor xor_1 (xor_1_out, OF, SF);
  not not_1 (not_1_out, xor_1_out);
  not not_2 (not_2_out, ZF);
  and and_1 (and_1_out, not_1_out, not_2_out);
  not not_3 (not_3_out, xor_1_out);
  Multiplexer #(.select(4)) multiplexer_1 (
    .in0(1'b1), .in1(or_1_out), .in2(xor_1_out), .in3(ZF), .in4(not_2_out), .in5(not_3_out), .in6(and_1_out),
    .in7(1'b1), .in8(1'b1), .in9(1'b1), .in10(1'b1), .in11(1'b1), .in12(1'b1), .in13(1'b1), .in14(1'b1),
    .in15(1'b1), .out(CC), .sel(ifun));  // open: en
endmodule

module Memory (
  input  [31:0] ValE_0,
  input  [31:0] ValE_1,
  input  [31:0] ValA_0,
  input  [31:0] ValA_1,
  input  [31:0] ValP,
  input  [3:0] iCode,
  output [31:0] Addr_0,
  output [31:0] Data_0,
  output [31:0] Addr_1,
  output [31:0] Data_1,
  output Read,
  output Write
);

  Memory_helper memory_helper_1 (
    .ValE(ValE_0), .ValA(ValA_0), .ValP(ValP), .iCode(iCode), .Addr(Addr_0), .Data(Data_0));
  Memory_helper memory_helper_2 (
    .ValE(ValE_1), .ValA(ValA_1), .ValP(ValP), .iCode(iCode), .Addr(Addr_1), .Data(Data_1));
  read_write__mem read_write_mem_1 (.iCode(iCode), .Read(Read), .Write(Write));
endmodule

module Memory_helper (
  input  [31:0] ValE,
  input  [31:0] ValA,
  input  [31:0] ValP,
  input  [3:0] iCode,
  output [31:0] Addr,
  output [31:0] Data
);

  Multiplexer #(.select(4), .width(32)) multiplexer_1 (
    .in0({32{1'b0}}), .in1({32{1'b0}}), .in2({32{1'b0}}), .in3({32{1'b0}}), .in4(ValE), .in5(ValE),
    .in6({32{1'b0}}), .in7({32{1'b0}}), .in8(ValE), .in9(ValA), .in10(ValE), .in11(ValA), .in12({32{1'b0}}),
    .in13({32{1'b0}}), .in14({32{1'b0}}), .in15({32{1'b0}}), .out(Addr), .sel(iCode));  // open: en
  Multiplexer #(.select(4), .width(32)) multiplexer_2 (
    .in0({32{1'b0}}), .in1({32{1'b0}}), .in2({32{1'b0}}), .in3({32{1'b0}}), .in4(ValA), .in5({32{1'b0}}),
    .in6({32{1'b0}}), .in7({32{1'b0}}), .in8(ValP), .in9({32{1'b0}}), .in10(ValA), .in11({32{1'b0}}),
    .in12({32{1'b0}}), .in13({32{1'b0}}), .in14({32{1'b0}}), .in15({32{1'b0}}), .out(Data), .sel(iCode));  // open: en
endmodule

module read_write__mem (
  input  [3:0] iCode,
  output Read,
  output Write
);

  Multiplexer #(.select(4)) multiplexer_1 (
    .in0(1'b0), .in1(1'b0), .in2(1'b0), .in3(1'b0), .in4(1'b0), .in5(1'b1), .in6(1'b0), .in7(1'b0),
    .in8(1'b0), .in9(1'b1), .in10(1'b0), .in11(1'b1), .in12(1'b0), .in13(1'b0), .in14(1'b0), .in15(1'b0),
    .out(Read), .sel(iCode));  // open: en
  Multiplexer #(.select(4)) multiplexer_2 (
    .in0(1'b0), .in1(1'b0), .in2(1'b0), .in3(1'b0), .in4(1'b1), .in5(1'b0), .in6(1'b0), .in7(1'b0),
    .in8(1'b1), .in9(1'b0), .in10(1'b1), .in11(1'b0), .in12(1'b0), .in13(1'b0), .in14(1'b0), .in15(1'b0),
    .out(Write), .sel(iCode));  // open: en
endmodule

module PC (
  input  [31:0] ValP,
  input  [31:0] ValC_0,
  input  CC,
  input  [31:0] ValM_0,
  input  [3:0] iCode,
  output [31:0] NextPC_0
);

  PC_helper pc_helper_1 (.ValP(ValP), .ValC(ValC_0), .ValM(ValM_0), .CC(CC), .iCode(iCode), .NextPC(NextPC_0));
endmodule

module PC_helper (
  input  [31:0] ValP,
  input  [31:0] ValC,
  input  [31:0] ValM,
  input  CC,
  input  [3:0] iCode,
  output [31:0] NextPC
);

  wire [31:0] multiplexer_1_out;

  Multiplexer #(.width(32)) multiplexer_1 (.in0(ValP), .in1(ValC), .out(multiplexer_1_out), .sel(CC));  // open: en
  Multiplexer #(.select(4), .width(32)) multiplexer_2 (
    .in0(ValP), .in1(ValP), .in2(ValP), .in3(ValP), .in4(ValP), .in5(ValP), .in6(ValP),
    .in7(multiplexer_1_out), .in8(ValC), .in9(ValM), .in10(ValP), .in11(ValP), .in12(ValP), .in13(ValP),
    .in14(ValP), .in15(ValP), .out(NextPC), .sel(iCode));  // open: en
endmodule

module stat_helper (
  input  ins_inv,
  input  imemrr,
  input  dmemrr,
  input  [3:0] icode,
  output [1:0] statuscode
);

  wire and_1_out, and_2_out, not_1_out, not_2_out, not_3_out, not_4_out, not_5_out, or_1_out;

  or or_1 (or_1_out, imemrr, dmemrr);
  not not_1 (not_1_out, icode[0]);
  not not_2 (not_2_out, icode[1]);
  not not_3 (not_3_out, icode[2]);
  not not_4 (not_4_out, icode[3]);
  and and_1 (and_1_out, not_1_out, not_2_out, not_3_out, not_4_out);
  not not_5 (not_5_out, ins_inv);
  and and_2 (and_2_out, not_5_out, or_1_out);
  or or_2 (statuscode[1], and_2_out, and_1_out);
  or or_3 (statuscode[0], ins_inv, and_1_out);
endmodule
